# Fritzing sketch Draze_scheme (saved by Fritzing 0.9.4)

parts:
  K1 = Relay [part_number=FRS1B-S package=THT]
  K2 = Relay [part_number=FRS1B-S package=THT]
  K3 = Relay [part_number=FRS1B-S package=THT]
  DS1 = DS18B20 1-Wire Temperature Sensor [part_number=DS18B20]
  Part2 = Adafruit I2C+SPI LCD Backpack [part_number="Adafruit #292"]
  RE1 = KY-040 Rotary encoder [package=THT]
  HLK-PM1 = HLK-PM01
  S6 = SWITCH-MOMENTARY-2 [package=tactile_switch_tall]
  S7 = SWITCH-MOMENTARY-2 [package=tactile_switch_tall]
  S8 = SWITCH-MOMENTARY-2 [package=tactile_switch_tall]
  LED4 = smd LED [color="Red (633nm)" package="0805 [SMD]"]
  LED5 = smd LED [color="Red (633nm)" package="0805 [SMD]"]
  LED6 = smd LED [color="Red (633nm)" package="0805 [SMD]"]
  R6 = Resistor [tolerance=±5% resistance=220 package="0402 [SMD]"]
  R7 = Resistor [tolerance=±5% resistance=220 package="0402 [SMD]"]
  R8 = Resistor [tolerance=±5% resistance=220 package="0402 [SMD]"]
  U1 = ESP32-38PinWide [part_number=ESP32-38PinWide]

nets:
  N1: K1.A, U1.GPIO18
  N2: K1.COIL2, K2.COIL2, K3.COIL2, HLK-PM1.AC#0
  GND: K1.B, K2.B, K3.B, DS1.GND, Part2.GND, RE1.GND, LED4.cathode, LED5.cathode, LED6.cathode
  N3: K2.A, U1.GPIO19
  N4: K3.A, U1.GPIO21
  N5: DS1.DQ, U1.GPIO26
  N6: DS1.VDD, U1.3.3
  N7: Part2.CLOCK, U1.GPIO25
  N8: Part2.DATA, U1.GPIO33
  VCC: Part2.VCC, U1.VIN
  N9: RE1.SW, U1.GPIO27
  N10: RE1.DT, U1.GPIO14
  N11: RE1.CLK, U1.GPIO12
  N12: HLK-PM1.AC#1, S6.2, S7.2, S8.2
  N13: S6.1, U1.GPIO5
  N14: S7.1, U1.GPIO17
  N15: S8.1, U1.GPIO16
  N16: LED4.anode, R6.Pin_1
  N17: LED5.anode, R7.Pin_1
  N18: LED6.anode, R8.Pin_1
  N19: R6.Pin_0, U1.GPIO2
  N20: R7.Pin_0, U1.GPIO15
  N21: R8.Pin_0, U1.GPIO0

custom parts:
  Adafruit I2C+SPI LCD Backpack: LCD backpacks reduce the number of pins needed to connect to an LCD. LCDs are a fun and easy way to have your microcontroller project talk back to you. Character LCDs are common, and easy to get, available in tons of colors and sizes. We've written tutorials on using character LCDs with an Arduino (or similar microcontroller) but find that the number of pins necessary to control the LCD can be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
  KY-040 Rotary encoder: KY-040 Rotary Encoder with switch on breakout borad from AZ Delivery
  ESP32-38PinWide: Generic 38-Pin ESP32 with wide format (only access to one side of pins on a breadboard) based on Stephen Lilley's HiLetgo ESP-WROOM-32 ESP32 ESP-32S Development Board.
