# Fritzing sketch Draze_scheme (saved by Fritzing 0.9.5d)

parts:
  RE1 = KY-040 Rotary encoder [package=THT]
  U1 = ESP32-38PinWide [part_number=ESP32-38PinWide]
  LCD2004-I2C1 = LCD2004-I2C
  Fan = AC Power [voltage=220 frequency=60]
  Cold = AC Power [voltage=220 frequency=60]
  Heat = AC Power [voltage=220 frequency=60]
  S13 = SWITCH-MOMENTARY-2 [package=tactile-switch-1101ne]
  J1 = Piezo Speaker
  Q1 = NPN-Transistor [package="SOT-23 [SMD]"]
  DS2 = DS18B20 1-Wire Temperature Sensor [part_number=DS18B20]
  Power_plug1 = Power plug
  ZS-042_RTC1 = ZS-042 RTC Module
  U5 = RELAY [package=OJ]
  U6 = RELAY [package=OJ]
  U7 = RELAY [package=OJ]
  R1 = Resistor [tolerance=±5% resistance=4.7k package="2512 [SMD]"]
  btn1 = Round Pushbutton
  S15 = Toggle Switch [package=THT]
  R2 = Resistor [tolerance=±5% power=0.25W resistance=10k package=THT]
  btn3 = Round Pushbutton
  R3 = Resistor [tolerance=±5% power=0.25W resistance=10k package=THT]
  R4 = Resistor [tolerance=±5% power=0.25W resistance=10k package=THT]
  btn2 = Round Pushbutton
  LED_LCD = Super Flux LED blue [color=Green]
  LEDSBTN = Super Flux RGB LED (com. cathode)
  SW1 = DIP SWITCH [package=dipswitch-02]
  SW2 = DIP SWITCH [package=dipswitch-02]
  R5 = Temperature Sensor (Thermistor) [thermistor_type=NTC package=THT]
  R6 = Resistor [tolerance=±10% resistance=10k power=0.25W package=THT]

nets:
  GND: RE1.GND, U1.GND, S13.2, Q1.2, DS2.GND, Power_plug1.GND, ZS-042_RTC1.GND#0, U5.MAIN, U6.MAIN, U7.MAIN, btn1.leg1, btn3.leg1, btn2.leg1, LED_LCD.cathode, LEDSBTN.common_cathode, R6.Pin_1
  5V: RE1.Vcc, J1.pin2, DS2.VDD, ZS-042_RTC1.VCC#1, R1.Pin_1, S15.COM, R2.Pin_1, R3.Pin_1, R4.Pin_1
  N1: RE1.SW, U1.GPIO36
  N2: RE1.DT, U1.GPIO39
  N3: RE1.CLK, U1.GPIO34
  N4: U1.3.3, Power_plug1.VCC
  N5: U1.EN, S13.1
  RTC_ALARM: U1.GPIO35
  BTN3: U1.GPIO32
  RELAY2: U1.GPIO33, U6.NO
  N6: U1.GPIO25, Q1.0
  N7: U1.GPIO26, R5.pin_0
  RELAY3: U1.GPIO27, U5.NO
  PWMSTART: U1.GPIO14
  ?NO?: U1.GPIO12
  SENSOR_ONEWIRE: U1.GPIO13, DS2.DQ, R1.Pin_0
  NO: U1.GPIO9, U1.GPIO10, U1.GPIO11, U1.GPIO6, U1.GPIO7, U1.GPIO8, U1.GPIO0
  N8: U1.VIN, S15.L2
  coreDebug: U1.GPIO15
  ledBuiltIn: U1.GPIO2
  LED2: U1.GPIO4, LEDSBTN.green_anode
  BTN1/RX2: U1.GPIO16
  LED1/TX2: U1.GPIO17, LEDSBTN.red_anode
  LED_LCD: U1.GPIO5, LED_LCD.anode
  BTN2: U1.GPIO18
  RELAY1: U1.GPIO19, U7.NO
  SDA: U1.GPIO21, ZS-042_RTC1.SDA#2
  RX: U1.GPIO3
  TX: U1.GPIO1
  SCL: U1.GPIO22, ZS-042_RTC1.SCL#3
  LED3: U1.GPIO23, LEDSBTN.blue_anode
  N9: LCD2004-I2C1.GND, ZS-042_RTC1.GND#6
  N10: LCD2004-I2C1.VCC, ZS-042_RTC1.VCC#7
  N11: LCD2004-I2C1.SDA, ZS-042_RTC1.SDA#8
  N12: LCD2004-I2C1.SCL, ZS-042_RTC1.SCL#9
  N13: Fan.V+, U7.COIL1
  N14: Fan.V-, U7.COIL2
  N15: Cold.V+, U6.COIL1
  N16: Cold.V-, U6.COIL2
  N17: Heat.V+, U5.COIL1
  N18: Heat.V-, U5.COIL2
  N19: J1.pin1, Q1.1
  N20: btn1.leg0, SW1.3
  floating: S15.L1
  N21: R2.Pin_0, SW1.2
  N22: btn3.leg0, SW1.4
  N23: R3.Pin_0, SW1.1
  N24: R4.Pin_0, SW2.1
  N25: btn2.leg0, SW2.4
  NOTREAL: SW2.2, SW2.3
  N26: R5.pin_1, R6.Pin_0

custom parts:
  KY-040 Rotary encoder: KY-040 Rotary Encoder with switch on breakout borad from AZ Delivery
  ESP32-38PinWide: Generic 38-Pin ESP32 with wide format (only access to one side of pins on a breadboard) based on Stephen Lilley's HiLetgo ESP-WROOM-32 ESP32 ESP-32S Development Board.
  LCD2004-I2C: A standard character display with 4x20 characters. Comes in many colors with LCM2004 IIC attached.
